# Fritzing sketch bitx40_prototype (saved by Fritzing 0.9.3b)
circuit board: 2.84872cm x 2.67186cm
breadboards: 1

parts:
  V1 = DC Power [voltage=5]
  R3 = Resistor [tolerance=±5% resistance=10k package=THT]
  R1 = Resistor [tolerance=±5% resistance=2.2k package=THT]
  R4 = Resistor [tolerance=±5% resistance=10k package=THT]
  Q1 = NPN-Transistor [part_number=2N3904 package="TO92 [THT]"]
  C9 = Capacitor [part_number=0.1uF package=cap-pth-small2]
  C1 = Electrolytic Capacitor [capacitance=1µF package="100 mil [THT, electrolytic]"]
  C7 = Capacitor [part_number=1000pF package=cap-pth-small2]
  C8 = Capacitor [part_number="1000 pF" package=cap-pth-small2]
  R5 = Resistor [tolerance=±5% resistance=1k package=THT]
  R2 = Resistor [tolerance=±5% resistance=10k package=THT]
  Q2 = NPN-Transistor [part_number=2N3904 package="TO92 [THT]"]
  J1 = female pin header, 2 pins [form="♀ (female)" part_number="5V alim"]
  J3 = female pin header, 2 pins [form="♀ (female)"]
  L1 = Inductor [inductance=9µH package="400 mil [THT]"]
  J2 = male pin header, 2 pins [form="♂ (male)" part_number="Var capa"]
  C6 = Capacitor [part_number="120 pF" package=cap-pth-small2]

nets:
  5V: V1.V+, R3.Pin_0, Q1.C, C1.+, Q2.C, J1.pin1
  GND: V1.V-, R1.Pin_1, C1.-, C8.2, R5.Pin_1, R2.Pin_1, J1.pin2, J3.pin2, J2.pin2, C6.2
  N1: R3.Pin_1, Q1.B, C7.1, R2.Pin_0, L1.pin_0
  N2: R1.Pin_0, R4.Pin_1, Q1.E
  N3: R4.Pin_0, Q2.B
  N4: C9.1, J3.pin1
  N5: C9.2, R5.Pin_0, Q2.E
  N6: C7.2, C8.1
  N7: L1.pin_1, J2.pin1, C6.1

notes:
  Variable capacitor
  100pF
  Output
  1kOhms
  ~1V
  ~7MHz
  +5V
  GND
  Osc+
  Osc-
